// Logisim project processador-8-bits.circ as structural Verilog: 13 circuits, main circuit FA
module FA (
  input  A,
  input  B,
  input  Cin,
  output S,
  output Cout
);

  wire and_1_out, and_2_out, xor_1_out;

  xor xor_1 (xor_1_out, A, B);
  xor xor_2 (S, xor_1_out, Cin);
  and and_1 (and_1_out, Cin, xor_1_out);
  and and_2 (and_2_out, A, B);
  or or_1 (Cout, and_1_out, and_2_out);
endmodule

module FA_4bits (
  input  A0,
  input  B0,
  input  Cin,
  input  A1,
  input  B1,
  input  A2,
  input  B2,
  input  A3,
  input  B3,
  output S0,
  output S1,
  output S2,
  output S3,
  output Cout
);

  wire fa_1_cout, fa_2_cout, fa_3_cout;

  FA fa_1 (.A(A0), .B(B0), .Cin(Cin), .S(S0), .Cout(fa_1_cout));
  FA fa_2 (.A(A1), .B(B1), .Cin(fa_1_cout), .S(S1), .Cout(fa_2_cout));
  FA fa_3 (.A(A2), .B(B2), .Cin(fa_2_cout), .S(S2), .Cout(fa_3_cout));
  FA fa_4 (.A(A3), .B(B3), .Cin(fa_3_cout), .S(S3), .Cout(Cout));
endmodule

module FA_8bits (
  input  A0,
  input  B0,
  input  A1,
  input  B1,
  input  A2,
  input  B2,
  input  A3,
  input  B3,
  input  A4,
  input  B4,
  input  A5,
  input  B5,
  input  A6,
  input  B6,
  input  A7,
  input  B7,
  output S0,
  output S1,
  output S2,
  output S3,
  output S4,
  output S5,
  output S6,
  output S7,
  output Cout
);

  wire fa_4bits_1_cout;

  FA_4bits fa_4bits_1 (
    .A0(A0), .B0(B0), .Cin(1'b0), .A1(A1), .B1(B1), .A2(A2), .B2(B2), .A3(A3), .B3(B3), .S0(S0), .S1(S1),
    .S2(S2), .S3(S3), .Cout(fa_4bits_1_cout));
  FA_4bits fa_4bits_2 (
    .A0(A4), .B0(B4), .Cin(fa_4bits_1_cout), .A1(A5), .B1(B5), .A2(A6), .B2(B6), .A3(A7), .B3(B7), .S0(S4),
    .S1(S5), .S2(S6), .S3(S7), .Cout(Cout));
endmodule

module subtrator_8bits (
  input  B0,
  input  B1,
  input  B2,
  input  B3,
  input  B4,
  input  B5,
  input  B6,
  input  B7,
  input  A0,
  input  A1,
  input  A2,
  input  A3,
  input  A4,
  input  A5,
  input  A6,
  input  A7,
  output S0,
  output S1,
  output S2,
  output S3,
  output S4,
  output S5,
  output S6,
  output S7,
  output Cout
);

  wire fa_8bits_1_cout, fa_8bits_1_s0, fa_8bits_1_s1, fa_8bits_1_s2, fa_8bits_1_s3, fa_8bits_1_s4,
       fa_8bits_1_s5, fa_8bits_1_s6, fa_8bits_1_s7, not_1_out, not_2_out, not_3_out, not_4_out, not_5_out,
       not_6_out, not_7_out, not_8_out;

  not not_1 (not_1_out, A0);
  not not_2 (not_2_out, A1);
  not not_3 (not_3_out, A2);
  not not_4 (not_4_out, A3);
  not not_5 (not_5_out, A4);
  not not_6 (not_6_out, A5);
  not not_7 (not_7_out, A6);
  not not_8 (not_8_out, A7);
  FA_8bits fa_8bits_1 (
    .A0(not_1_out), .B0(1'b1), .A1(not_2_out), .B1(1'b0), .A2(not_3_out), .B2(1'b0), .A3(not_4_out),
    .B3(1'b0), .A4(not_5_out), .B4(1'b0), .A5(not_6_out), .B5(1'b0), .A6(not_7_out), .B6(1'b0),
    .A7(not_8_out), .B7(1'b0), .S0(fa_8bits_1_s0), .S1(fa_8bits_1_s1), .S2(fa_8bits_1_s2),
    .S3(fa_8bits_1_s3), .S4(fa_8bits_1_s4), .S5(fa_8bits_1_s5), .S6(fa_8bits_1_s6), .S7(fa_8bits_1_s7),
    .Cout(fa_8bits_1_cout));
  FA_8bits fa_8bits_2 (
    .A0(fa_8bits_1_s0), .B0(B0), .A1(fa_8bits_1_s1), .B1(B1), .A2(fa_8bits_1_s2), .B2(B2),
    .A3(fa_8bits_1_s3), .B3(B3), .A4(fa_8bits_1_s4), .B4(B4), .A5(fa_8bits_1_s5), .B5(B5),
    .A6(fa_8bits_1_s6), .B6(B6), .A7(fa_8bits_1_s7), .B7(B7), .S0(S0), .S1(S1), .S2(S2), .S3(S3), .S4(S4),
    .S5(S5), .S6(S6), .S7(S7), .Cout(Cout));
  // also tied to GND on the sheet: fa_8bits_1_cout
endmodule

module main (
  input  OP2,
  input  OP1,
  input  OP0,
  input  A0,
  input  B0,
  input  A1,
  input  B1,
  input  A2,
  input  B2,
  input  A3,
  input  B3,
  input  A4,
  input  B4,
  input  A5,
  input  B5,
  input  A6,
  input  B6,
  input  A7,
  input  B7
);

  wire hexa_to_7_display_1_out_a, hexa_to_7_display_1_out_b, hexa_to_7_display_1_out_c,
       hexa_to_7_display_1_out_d, hexa_to_7_display_1_out_e, hexa_to_7_display_1_out_f,
       hexa_to_7_display_1_out_g, hexa_to_7_display_2_out_a, hexa_to_7_display_2_out_b,
       hexa_to_7_display_2_out_c, hexa_to_7_display_2_out_d, hexa_to_7_display_2_out_e,
       hexa_to_7_display_2_out_f, hexa_to_7_display_2_out_g, ula_8_bits_opcodes_1_bt,
       ula_8_bits_opcodes_1_c0, ula_8_bits_opcodes_1_c1, ula_8_bits_opcodes_1_c2, ula_8_bits_opcodes_1_c3,
       ula_8_bits_opcodes_1_c4, ula_8_bits_opcodes_1_c5, ula_8_bits_opcodes_1_c6, ula_8_bits_opcodes_1_c7,
       ula_8_bits_opcodes_1_cout, ula_8_bits_opcodes_1_eq, ula_8_bits_opcodes_1_lt;

  ULA_8_bits_opcodes ula_8_bits_opcodes_1 (
    .Op2(OP2), .Op1(OP1), .Op0(OP0), .A0(A0), .B0(B0), .A1(A1), .B1(B1), .A2(A2), .B2(B2), .A3(A3), .B3(B3),
    .A4(A4), .B4(B4), .A5(A5), .B5(B5), .A6(A6), .B6(B6), .A7(A7), .B7(B7), .C0(ula_8_bits_opcodes_1_c0),
    .C1(ula_8_bits_opcodes_1_c1), .C2(ula_8_bits_opcodes_1_c2), .C3(ula_8_bits_opcodes_1_c3),
    .C4(ula_8_bits_opcodes_1_c4), .C5(ula_8_bits_opcodes_1_c5), .LT(ula_8_bits_opcodes_1_lt),
    .EQ(ula_8_bits_opcodes_1_eq), .BT(ula_8_bits_opcodes_1_bt), .C6(ula_8_bits_opcodes_1_c6),
    .C7(ula_8_bits_opcodes_1_c7), .Cout(ula_8_bits_opcodes_1_cout));
  hexa_to_7_display hexa_to_7_display_1 (
    .iA(ula_8_bits_opcodes_1_c0), .iB(ula_8_bits_opcodes_1_c1), .iC(ula_8_bits_opcodes_1_c2),
    .iD(ula_8_bits_opcodes_1_c3), .out_A(hexa_to_7_display_1_out_a), .out_B(hexa_to_7_display_1_out_b),
    .out_C(hexa_to_7_display_1_out_c), .out_D(hexa_to_7_display_1_out_d), .out_E(hexa_to_7_display_1_out_e),
    .out_F(hexa_to_7_display_1_out_f), .out_G(hexa_to_7_display_1_out_g));
  hexa_to_7_display hexa_to_7_display_2 (
    .iA(ula_8_bits_opcodes_1_c4), .iB(ula_8_bits_opcodes_1_c5), .iC(ula_8_bits_opcodes_1_c6),
    .iD(ula_8_bits_opcodes_1_c7), .out_A(hexa_to_7_display_2_out_a), .out_B(hexa_to_7_display_2_out_b),
    .out_C(hexa_to_7_display_2_out_c), .out_D(hexa_to_7_display_2_out_d), .out_E(hexa_to_7_display_2_out_e),
    .out_F(hexa_to_7_display_2_out_f), .out_G(hexa_to_7_display_2_out_g));
  _7_Segment_Display u_7_segment_display_1 (
    .g(hexa_to_7_display_1_out_g), .f(hexa_to_7_display_1_out_f), .a(hexa_to_7_display_1_out_a),
    .b(hexa_to_7_display_1_out_b), .e(hexa_to_7_display_1_out_e), .d(hexa_to_7_display_1_out_d),
    .c(hexa_to_7_display_1_out_c));  // open: dp
  LED LT (.in(ula_8_bits_opcodes_1_lt));
  LED EQ (.in(ula_8_bits_opcodes_1_eq));
  LED BT (.in(ula_8_bits_opcodes_1_bt));
  _7_Segment_Display u_7_segment_display_2 (
    .g(hexa_to_7_display_2_out_g), .f(hexa_to_7_display_2_out_f), .a(hexa_to_7_display_2_out_a),
    .b(hexa_to_7_display_2_out_b), .e(hexa_to_7_display_2_out_e), .d(hexa_to_7_display_2_out_d),
    .c(hexa_to_7_display_2_out_c));  // open: dp
  // also tied to GND on the sheet: ula_8_bits_opcodes_1_cout

  // Notes on the sheet:
  //   0 0 0 = Soma
  //   1 0 0 = Sub
  //   0 1 0 = Multi
  //   1 1 0 = Comp
  //   0 0 1 = Shift
endmodule

module comparador_1_bit (
  input  A,
  input  B,
  input  in_LT,
  input  in_Eq,
  input  in_Bt,
  output LT,
  output EQ,
  output BT
);

  wire and_1_out, and_2_out, and_3_out, and_4_out, and_5_out, and_6_out, and_7_out, and_8_out, not_1_out,
       not_2_out;

  not not_1 (not_1_out, A);
  not not_2 (not_2_out, B);
  and and_1 (and_1_out, not_1_out, B);
  and and_2 (and_2_out, not_1_out, in_LT);
  and and_3 (and_3_out, B, in_LT);
  and and_4 (and_4_out, not_1_out, not_2_out, in_Eq);
  and and_5 (and_5_out, A, B, in_Eq);
  and and_6 (and_6_out, A, not_2_out);
  and and_7 (and_7_out, not_2_out, in_Bt);
  and and_8 (and_8_out, A, in_Bt);
  or or_1 (LT, and_1_out, and_2_out, and_3_out);
  or or_2 (EQ, and_4_out, and_5_out);
  or or_3 (BT, and_6_out, and_7_out, and_8_out);
endmodule

module comparador_8_bits (
  input  A0,
  input  B0,
  input  A1,
  input  B1,
  input  A2,
  input  B2,
  input  A3,
  input  B3,
  input  A4,
  input  B4,
  input  A5,
  input  B5,
  input  A6,
  input  B6,
  input  A7,
  input  B7,
  output LT,
  output EQ,
  output BT
);

  wire comparador_1_bit_1_bt, comparador_1_bit_1_eq, comparador_1_bit_1_lt, comparador_1_bit_2_bt,
       comparador_1_bit_2_eq, comparador_1_bit_2_lt, comparador_1_bit_3_bt, comparador_1_bit_3_eq,
       comparador_1_bit_3_lt, comparador_1_bit_4_bt, comparador_1_bit_4_eq, comparador_1_bit_4_lt,
       comparador_1_bit_5_bt, comparador_1_bit_5_eq, comparador_1_bit_5_lt, comparador_1_bit_6_bt,
       comparador_1_bit_6_eq, comparador_1_bit_6_lt, meio_comparador_1_bt, meio_comparador_1_eq,
       meio_comparador_1_lt;

  meio_comparador meio_comparador_1 (
    .A(A0), .B(B0), .LT(meio_comparador_1_lt), .EQ(meio_comparador_1_eq), .BT(meio_comparador_1_bt));
  comparador_1_bit comparador_1_bit_1 (
    .A(A1), .B(B1), .in_LT(meio_comparador_1_lt), .in_Eq(meio_comparador_1_eq), .in_Bt(meio_comparador_1_bt),
    .LT(comparador_1_bit_1_lt), .EQ(comparador_1_bit_1_eq), .BT(comparador_1_bit_1_bt));
  comparador_1_bit comparador_1_bit_2 (
    .A(A2), .B(B2), .in_LT(comparador_1_bit_1_lt), .in_Eq(comparador_1_bit_1_eq),
    .in_Bt(comparador_1_bit_1_bt), .LT(comparador_1_bit_2_lt), .EQ(comparador_1_bit_2_eq),
    .BT(comparador_1_bit_2_bt));
  comparador_1_bit comparador_1_bit_3 (
    .A(A3), .B(B3), .in_LT(comparador_1_bit_2_lt), .in_Eq(comparador_1_bit_2_eq),
    .in_Bt(comparador_1_bit_2_bt), .LT(comparador_1_bit_3_lt), .EQ(comparador_1_bit_3_eq),
    .BT(comparador_1_bit_3_bt));
  comparador_1_bit comparador_1_bit_4 (
    .A(A4), .B(B4), .in_LT(comparador_1_bit_3_lt), .in_Eq(comparador_1_bit_3_eq),
    .in_Bt(comparador_1_bit_3_bt), .LT(comparador_1_bit_4_lt), .EQ(comparador_1_bit_4_eq),
    .BT(comparador_1_bit_4_bt));
  comparador_1_bit comparador_1_bit_5 (
    .A(A5), .B(B5), .in_LT(comparador_1_bit_4_lt), .in_Eq(comparador_1_bit_4_eq),
    .in_Bt(comparador_1_bit_4_bt), .LT(comparador_1_bit_5_lt), .EQ(comparador_1_bit_5_eq),
    .BT(comparador_1_bit_5_bt));
  comparador_1_bit comparador_1_bit_6 (
    .A(A6), .B(B6), .in_LT(comparador_1_bit_5_lt), .in_Eq(comparador_1_bit_5_eq),
    .in_Bt(comparador_1_bit_5_bt), .LT(comparador_1_bit_6_lt), .EQ(comparador_1_bit_6_eq),
    .BT(comparador_1_bit_6_bt));
  comparador_1_bit comparador_1_bit_7 (
    .A(A7), .B(B7), .in_LT(comparador_1_bit_6_lt), .in_Eq(comparador_1_bit_6_eq),
    .in_Bt(comparador_1_bit_6_bt), .LT(LT), .EQ(EQ), .BT(BT));
endmodule

module meio_comparador (
  input  A,
  input  B,
  output LT,
  output EQ,
  output BT
);

  wire not_1_out, not_2_out;

  not not_1 (not_1_out, A);
  not not_2 (not_2_out, B);
  and and_1 (LT, not_1_out, B);
  xnor xnor_1 (EQ, A, B);
  and and_2 (BT, A, not_2_out);
endmodule

module bit_shift (
  input  A0,
  input  A1,
  input  A2,
  input  A3,
  input  A4,
  input  A5,
  input  A6,
  input  A7,
  input  Clean,
  output C0,
  output C1,
  output C2,
  output C3,
  output C4,
  output C5,
  output C6,
  output C7,
  output Cout
);

  wire clock_1_out;

  and and_1 (C0, 1'b0, A0);
  Clock clock_1 (.out(clock_1_out));
  D_Flip_Flop d_ff_1 (.D(A0), .clk(clock_1_out), .Q(C1), .reset(Clean));  // open: Qn, preset
  D_Flip_Flop d_ff_2 (.D(A1), .clk(clock_1_out), .Q(C2), .reset(Clean));  // open: Qn, preset
  D_Flip_Flop d_ff_3 (.D(A2), .clk(clock_1_out), .Q(C3), .reset(Clean));  // open: Qn, preset
  D_Flip_Flop d_ff_4 (.D(A3), .clk(clock_1_out), .Q(C4), .reset(Clean));  // open: Qn, preset
  D_Flip_Flop d_ff_5 (.D(A4), .clk(clock_1_out), .Q(C5), .reset(Clean));  // open: Qn, preset
  D_Flip_Flop d_ff_6 (.D(A5), .clk(clock_1_out), .Q(C6), .reset(Clean));  // open: Qn, preset
  D_Flip_Flop d_ff_7 (.D(A6), .clk(clock_1_out), .Q(C7), .reset(Clean));  // open: Qn, preset
  D_Flip_Flop d_ff_8 (.D(A7), .clk(clock_1_out), .Q(Cout), .reset(Clean));  // open: Qn, preset
endmodule

module multiplicador_8_bits (
  input  A0,
  input  B0,
  input  A1,
  input  B1,
  input  B2,
  input  A2,
  input  B3,
  input  A3,
  output C7,
  output C6,
  output C5,
  output C4,
  output C3,
  output C2,
  output C1,
  output C0
);

  wire and_1_out, and_2_out, and_3_out, and_4_out, and_5_out, and_6_out, and_7_out, and_8_out, and_9_out,
       and_10_out, and_11_out, and_12_out, and_13_out, and_14_out, and_15_out, fa_4bits_2_cout,
       fa_4bits_2_s1, fa_4bits_2_s2, fa_4bits_2_s3, fa_4bits_3_cout, fa_4bits_3_s1, fa_4bits_3_s2,
       fa_4bits_3_s3;

  and and_1 (and_1_out, A3, B2);
  and and_2 (and_2_out, A3, B3);
  and and_3 (and_3_out, A3, B1);
  and and_4 (and_4_out, A3, B0);
  and and_5 (and_5_out, A2, B3);
  FA_4bits fa_4bits_1 (
    .A0(fa_4bits_2_s1), .B0(and_4_out), .A1(fa_4bits_2_s2), .B1(and_3_out), .A2(fa_4bits_2_s3),
    .B2(and_1_out), .A3(fa_4bits_2_cout), .B3(and_2_out), .S0(C3), .S1(C4), .S2(C5), .S3(C6), .Cout(C7));  // open: Cin
  and and_6 (and_6_out, A2, B2);
  and and_7 (and_7_out, A2, B1);
  and and_8 (and_8_out, A2, B0);
  and and_9 (and_9_out, A1, B3);
  FA_4bits fa_4bits_2 (
    .A0(fa_4bits_3_s1), .B0(and_8_out), .A1(fa_4bits_3_s2), .B1(and_7_out), .A2(fa_4bits_3_s3),
    .B2(and_6_out), .A3(fa_4bits_3_cout), .B3(and_5_out), .S0(C2), .S1(fa_4bits_2_s1), .S2(fa_4bits_2_s2),
    .S3(fa_4bits_2_s3), .Cout(fa_4bits_2_cout));  // open: Cin
  and and_10 (and_10_out, A1, B2);
  and and_11 (and_11_out, A1, B1);
  and and_12 (and_12_out, A1, B0);
  and and_13 (and_13_out, A0, B3);
  FA_4bits fa_4bits_3 (
    .A0(and_15_out), .B0(and_12_out), .Cin(1'b0), .A1(and_14_out), .B1(and_11_out), .A2(and_13_out),
    .B2(and_10_out), .A3(1'b0), .B3(and_9_out), .S0(C1), .S1(fa_4bits_3_s1), .S2(fa_4bits_3_s2),
    .S3(fa_4bits_3_s3), .Cout(fa_4bits_3_cout));
  and and_14 (and_14_out, A0, B2);
  and and_15 (and_15_out, A0, B1);
  and and_16 (C0, A0, B0);
endmodule

module ULA_8_bits_opcodes (
  input  Op2,
  input  Op1,
  input  Op0,
  input  A0,
  input  B0,
  input  A1,
  input  B1,
  input  A2,
  input  B2,
  input  A3,
  input  B3,
  input  A4,
  input  B4,
  input  A5,
  input  B5,
  input  A6,
  input  B6,
  input  A7,
  input  B7,
  output C0,
  output C1,
  output C2,
  output C3,
  output C4,
  output C5,
  output LT,
  output EQ,
  output BT,
  output C6,
  output C7,
  output Cout
);

  wire and_1_out, and_2_out, and_3_out, and_4_out, and_5_out, and_6_out, and_7_out, and_8_out, and_9_out,
       and_10_out, and_11_out, and_12_out, and_13_out, and_14_out, and_15_out, and_16_out, and_17_out,
       and_18_out, and_19_out, and_20_out, and_21_out, and_22_out, and_23_out, and_24_out, and_25_out,
       and_26_out, and_27_out, and_28_out, and_29_out, and_30_out, and_31_out, and_32_out, and_33_out,
       and_34_out, and_35_out, and_36_out, and_37_out, and_38_out, and_39_out, and_40_out, and_41_out,
       and_42_out, and_43_out, and_44_out, and_45_out, and_46_out, and_47_out, and_48_out, and_49_out,
       and_50_out, and_51_out, and_52_out, and_53_out, and_54_out, and_55_out, and_56_out, and_57_out,
       and_58_out, and_59_out, and_60_out, and_61_out, and_62_out, and_63_out, and_64_out, bit_shift_1_c0,
       bit_shift_1_c1, bit_shift_1_c2, bit_shift_1_c3, bit_shift_1_c4, bit_shift_1_c5, bit_shift_1_c6,
       bit_shift_1_c7, bit_shift_1_cout, Comp_out, fa_8bits_1_cout, fa_8bits_1_s0, fa_8bits_1_s1,
       fa_8bits_1_s2, fa_8bits_1_s3, fa_8bits_1_s4, fa_8bits_1_s5, fa_8bits_1_s6, fa_8bits_1_s7, Mult_out,
       multiplicador_8_bits_1_c0, multiplicador_8_bits_1_c1, multiplicador_8_bits_1_c2,
       multiplicador_8_bits_1_c3, multiplicador_8_bits_1_c4, multiplicador_8_bits_1_c5,
       multiplicador_8_bits_1_c6, multiplicador_8_bits_1_c7, not_1_out, not_2_out, not_3_out, not_4_out,
       not_5_out, not_6_out, not_7_out, not_8_out, not_9_out, not_10_out, Shift_out, Sub_out,
       subtrator_8bits_1_cout, subtrator_8bits_1_s0, subtrator_8bits_1_s1, subtrator_8bits_1_s2,
       subtrator_8bits_1_s3, subtrator_8bits_1_s4, subtrator_8bits_1_s5, subtrator_8bits_1_s6,
       subtrator_8bits_1_s7, Sum_out;

  and and_1 (and_1_out, A0, Comp_out);
  and and_2 (and_2_out, B0, Comp_out);
  and and_3 (and_3_out, A1, Comp_out);
  and and_4 (and_4_out, B1, Comp_out);
  and and_5 (and_5_out, A2, Comp_out);
  and and_6 (and_6_out, B2, Comp_out);
  and and_7 (and_7_out, A3, Comp_out);
  and and_8 (and_8_out, B3, Comp_out);
  and and_9 (and_9_out, A4, Comp_out);
  and and_10 (and_10_out, B4, Comp_out);
  and and_11 (and_11_out, A5, Comp_out);
  and and_12 (and_12_out, B5, Comp_out);
  and and_13 (and_13_out, A6, Comp_out);
  and and_14 (and_14_out, B6, Comp_out);
  and and_15 (and_15_out, A7, Comp_out);
  and and_16 (and_16_out, B7, Comp_out);
  not not_1 (not_1_out, Op2);
  not not_2 (not_2_out, Op1);
  not not_3 (not_3_out, Op0);
  not not_4 (not_4_out, Op1);
  not not_5 (not_5_out, Op0);
  not not_6 (not_6_out, Op2);
  not not_7 (not_7_out, Op0);
  not not_8 (not_8_out, Op0);
  not not_9 (not_9_out, Op2);
  not not_10 (not_10_out, Op1);
  and Sum (Sum_out, not_1_out, not_2_out, not_3_out);
  and Sub (Sub_out, Op2, not_4_out, not_5_out);
  and Mult (Mult_out, not_6_out, Op1, not_7_out);
  and Comp (Comp_out, Op2, Op1, not_8_out);
  and Shift (Shift_out, not_9_out, not_10_out, Op0);
  comparador_8_bits comparador_8_bits_1 (
    .A0(and_1_out), .B0(and_2_out), .A1(and_3_out), .B1(and_4_out), .A2(and_5_out), .B2(and_6_out),
    .A3(and_7_out), .B3(and_8_out), .A4(and_9_out), .B4(and_10_out), .A5(and_11_out), .B5(and_12_out),
    .A6(and_13_out), .B6(and_14_out), .A7(and_15_out), .B7(and_16_out), .LT(LT), .EQ(EQ), .BT(BT));
  and and_17 (and_17_out, A0, Sum_out);
  and and_18 (and_18_out, B0, Sum_out);
  and and_19 (and_19_out, A1, Sum_out);
  and and_20 (and_20_out, B1, Sum_out);
  and and_21 (and_21_out, A2, Sum_out);
  and and_22 (and_22_out, B2, Sum_out);
  and and_23 (and_23_out, A3, Sum_out);
  and and_24 (and_24_out, B3, Sum_out);
  and and_25 (and_25_out, A4, Sum_out);
  and and_26 (and_26_out, B4, Sum_out);
  and and_27 (and_27_out, A5, Sum_out);
  and and_28 (and_28_out, B5, Sum_out);
  and and_29 (and_29_out, A6, Sum_out);
  and and_30 (and_30_out, B6, Sum_out);
  and and_31 (and_31_out, A7, Sum_out);
  and and_32 (and_32_out, B7, Sum_out);
  and and_33 (and_33_out, B0, Sub_out);
  and and_34 (and_34_out, B1, Sub_out);
  and and_35 (and_35_out, B2, Sub_out);
  and and_36 (and_36_out, B3, Sub_out);
  and and_37 (and_37_out, B4, Sub_out);
  and and_38 (and_38_out, B5, Sub_out);
  and and_39 (and_39_out, B6, Sub_out);
  and and_40 (and_40_out, B7, Sub_out);
  and and_41 (and_41_out, A0, Sub_out);
  and and_42 (and_42_out, A1, Sub_out);
  and and_43 (and_43_out, A2, Sub_out);
  and and_44 (and_44_out, A3, Sub_out);
  and and_45 (and_45_out, A4, Sub_out);
  and and_46 (and_46_out, A5, Sub_out);
  and and_47 (and_47_out, A6, Sub_out);
  and and_48 (and_48_out, A7, Sub_out);
  and and_49 (and_49_out, A0, Mult_out);
  and and_50 (and_50_out, B0, Mult_out);
  and and_51 (and_51_out, A1, Mult_out);
  and and_52 (and_52_out, B1, Mult_out);
  and and_53 (and_53_out, B2, Mult_out);
  and and_54 (and_54_out, A2, Mult_out);
  and and_55 (and_55_out, B3, Mult_out);
  and and_56 (and_56_out, A3, Mult_out);
  and and_57 (and_57_out, A0, Shift_out);
  and and_58 (and_58_out, A1, Shift_out);
  and and_59 (and_59_out, A2, Shift_out);
  and and_60 (and_60_out, A3, Shift_out);
  and and_61 (and_61_out, A4, Shift_out);
  and and_62 (and_62_out, A5, Shift_out);
  and and_63 (and_63_out, A6, Shift_out);
  and and_64 (and_64_out, A7, Shift_out);
  FA_8bits fa_8bits_1 (
    .A0(and_17_out), .B0(and_18_out), .A1(and_19_out), .B1(and_20_out), .A2(and_21_out), .B2(and_22_out),
    .A3(and_23_out), .B3(and_24_out), .A4(and_25_out), .B4(and_26_out), .A5(and_27_out), .B5(and_28_out),
    .A6(and_29_out), .B6(and_30_out), .A7(and_31_out), .B7(and_32_out), .S0(fa_8bits_1_s0),
    .S1(fa_8bits_1_s1), .S2(fa_8bits_1_s2), .S3(fa_8bits_1_s3), .S4(fa_8bits_1_s4), .S5(fa_8bits_1_s5),
    .S6(fa_8bits_1_s6), .S7(fa_8bits_1_s7), .Cout(fa_8bits_1_cout));
  subtrator_8bits subtrator_8bits_1 (
    .B0(and_33_out), .B1(and_34_out), .B2(and_35_out), .B3(and_36_out), .B4(and_37_out), .B5(and_38_out),
    .B6(and_39_out), .B7(and_40_out), .A0(and_41_out), .A1(and_42_out), .A2(and_43_out), .A3(and_44_out),
    .A4(and_45_out), .A5(and_46_out), .A6(and_47_out), .A7(and_48_out), .S0(subtrator_8bits_1_s0),
    .S1(subtrator_8bits_1_s1), .S2(subtrator_8bits_1_s2), .S3(subtrator_8bits_1_s3),
    .S4(subtrator_8bits_1_s4), .S5(subtrator_8bits_1_s5), .S6(subtrator_8bits_1_s6),
    .S7(subtrator_8bits_1_s7), .Cout(subtrator_8bits_1_cout));
  multiplicador_8_bits multiplicador_8_bits_1 (
    .A0(and_49_out), .B0(and_50_out), .A1(and_51_out), .B1(and_52_out), .B2(and_53_out), .A2(and_54_out),
    .B3(and_55_out), .A3(and_56_out), .C7(multiplicador_8_bits_1_c7), .C6(multiplicador_8_bits_1_c6),
    .C5(multiplicador_8_bits_1_c5), .C4(multiplicador_8_bits_1_c4), .C3(multiplicador_8_bits_1_c3),
    .C2(multiplicador_8_bits_1_c2), .C1(multiplicador_8_bits_1_c1), .C0(multiplicador_8_bits_1_c0));
  bit_shift bit_shift_1 (
    .A0(and_57_out), .A1(and_58_out), .A2(and_59_out), .A3(and_60_out), .A4(and_61_out), .A5(and_62_out),
    .A6(and_63_out), .A7(and_64_out), .C0(bit_shift_1_c0), .C1(bit_shift_1_c1), .C2(bit_shift_1_c2),
    .C3(bit_shift_1_c3), .C4(bit_shift_1_c4), .C5(bit_shift_1_c5), .C6(bit_shift_1_c6), .C7(bit_shift_1_c7),
    .Cout(bit_shift_1_cout));  // open: Clean
  or or_1 (C0, subtrator_8bits_1_s0, multiplicador_8_bits_1_c0, bit_shift_1_c0, fa_8bits_1_s0);
  or or_2 (C1, subtrator_8bits_1_s1, multiplicador_8_bits_1_c1, bit_shift_1_c1, fa_8bits_1_s1);
  or or_3 (C2, subtrator_8bits_1_s2, multiplicador_8_bits_1_c2, bit_shift_1_c2, fa_8bits_1_s2);
  or or_4 (C3, subtrator_8bits_1_s3, multiplicador_8_bits_1_c3, bit_shift_1_c3, fa_8bits_1_s3);
  or or_5 (C4, subtrator_8bits_1_s4, multiplicador_8_bits_1_c4, bit_shift_1_c4, fa_8bits_1_s4);
  or or_6 (C5, subtrator_8bits_1_s5, multiplicador_8_bits_1_c5, bit_shift_1_c5, fa_8bits_1_s5);
  or or_7 (C6, subtrator_8bits_1_s6, multiplicador_8_bits_1_c6, bit_shift_1_c6, fa_8bits_1_s6);
  or or_8 (C7, subtrator_8bits_1_s7, multiplicador_8_bits_1_c7, bit_shift_1_c7, fa_8bits_1_s7);
  or or_9 (Cout, subtrator_8bits_1_cout, bit_shift_1_cout, fa_8bits_1_cout);
endmodule

module hexa_to_7_display (
  input  iA,
  input  iB,
  input  iC,
  input  iD,
  output out_A,
  output out_B,
  output out_C,
  output out_D,
  output out_E,
  output out_F,
  output out_G
);

  wire and_1_out, and_2_out, and_3_out, and_4_out, and_5_out, and_6_out, and_7_out, and_8_out, and_9_out,
       and_10_out, and_11_out, and_12_out, and_13_out, and_14_out, and_15_out, and_16_out, and_17_out,
       and_18_out, and_19_out, and_20_out, and_21_out, and_22_out, and_23_out, and_24_out, and_25_out,
       and_26_out, and_27_out, and_28_out, and_29_out, and_30_out, and_31_out, and_32_out, and_33_out,
       and_34_out, and_35_out, and_36_out, and_37_out, and_38_out, and_39_out, and_40_out, and_41_out,
       not_1_out, not_2_out, not_3_out, not_4_out;

  not not_1 (not_1_out, iA);
  not not_2 (not_2_out, iB);
  not not_3 (not_3_out, iC);
  not not_4 (not_4_out, iD);
  and and_1 (and_1_out, not_2_out, not_4_out);
  and and_2 (and_2_out, not_1_out, iC);
  and and_3 (and_3_out, not_1_out, iB, iD);
  and and_4 (and_4_out, iA, not_2_out, not_3_out);
  and and_5 (and_5_out, iA, not_4_out);
  and and_6 (and_6_out, iB, iC);
  and and_7 (and_7_out, not_1_out, not_3_out, not_4_out);
  and and_8 (and_8_out, not_1_out, iC, iD);
  and and_9 (and_9_out, not_2_out, not_4_out);
  and and_10 (and_10_out, iA, not_3_out, iD);
  and and_11 (and_11_out, not_1_out, not_2_out);
  and and_12 (and_12_out, not_1_out, iB);
  and and_13 (and_13_out, iA, not_2_out);
  and and_14 (and_14_out, not_3_out, iD);
  and and_15 (and_15_out, not_1_out, not_3_out);
  and and_16 (and_16_out, not_1_out, iD);
  and and_17 (and_17_out, iB, not_3_out, iD);
  and and_18 (and_18_out, not_1_out, not_2_out, not_4_out);
  and and_19 (and_19_out, not_1_out, not_2_out, iC);
  and and_20 (and_20_out, not_1_out, iC, not_4_out);
  and and_21 (and_21_out, not_2_out, not_3_out, not_4_out);
  and and_22 (and_22_out, iA, not_2_out, iD);
  and and_23 (and_23_out, iA, not_3_out);
  and and_24 (and_24_out, iB, iC, not_4_out);
  and and_25 (and_25_out, not_1_out, not_2_out, not_4_out);
  and and_26 (and_26_out, iB, iD);
  and and_27 (and_27_out, iA, iD);
  and and_28 (and_28_out, iA, iB);
  and and_29 (and_29_out, not_2_out, iC, not_4_out);
  and and_30 (and_30_out, not_3_out, not_4_out);
  and and_31 (and_31_out, not_1_out, iB, not_3_out);
  and and_32 (and_32_out, iB, not_4_out);
  and and_33 (and_33_out, iA, not_2_out);
  and and_34 (and_34_out, iA, iC);
  and and_35 (and_35_out, not_2_out, iC);
  and and_36 (and_36_out, iA, not_2_out);
  and and_37 (and_37_out, not_1_out, iB, not_3_out);
  and and_38 (and_38_out, not_1_out, iB, not_4_out);
  and and_39 (and_39_out, iB, not_3_out, iD);
  and and_40 (and_40_out, iC, not_4_out);
  and and_41 (and_41_out, iA, iD);
  or or_1 (out_A, and_1_out, and_2_out, and_3_out, and_4_out, and_5_out, and_6_out);
  or or_2 (out_B, and_7_out, and_8_out, and_9_out, and_10_out, and_11_out);
  or or_3 (out_C, and_12_out, and_13_out, and_14_out, and_15_out, and_16_out);
  or or_4 (out_D, and_17_out, and_18_out, and_19_out, and_20_out, and_21_out, and_22_out, and_23_out, and_24_out);
  or or_5 (out_E, and_25_out, and_26_out, and_27_out, and_28_out, and_29_out);
  or or_6 (out_F, and_30_out, and_31_out, and_32_out, and_33_out, and_34_out);
  or or_7 (out_G, and_35_out, and_36_out, and_37_out, and_38_out, and_39_out, and_40_out, and_41_out);
endmodule

module register_4_BIT (
  input  A0,
  input  A1,
  input  A2,
  input  A3,
  output Q0,
  output Q1,
  output Q2,
  output Q3
);

  wire clock_1_out;

  Clock clock_1 (.out(clock_1_out));
  D_Flip_Flop d_ff_1 (.D(A0), .clk(clock_1_out), .Q(Q0));  // open: Qn, preset, reset
  D_Flip_Flop d_ff_2 (.D(A1), .clk(clock_1_out), .Q(Q1));  // open: Qn, preset, reset
  D_Flip_Flop d_ff_3 (.D(A2), .clk(clock_1_out), .Q(Q2));  // open: Qn, preset, reset
  D_Flip_Flop d_ff_4 (.D(A3), .clk(clock_1_out), .Q(Q3));  // open: Qn, preset, reset
endmodule
